// Logisim project CPU_design.circ as structural Verilog: 1 circuit, main circuit main
module main (
);

  wire clock_1_out;
  wire [3:0] controlled_buffer_1_out, controlled_buffer_1_out_2;
  wire [6:0] keyboard_1_data;
  wire [7:0] register_1_q, register_2_q;

  ROM rom_1 ();  // open: addr, data, sel
  Clock clock_1 (.out(clock_1_out));
  assign {controlled_buffer_1_out_2, controlled_buffer_1_out} = 1'b0 ? 8'h3 : 8'bz;  // Controlled_Buffer controlled_buffer_1
  Register register_1 (
    .D({controlled_buffer_1_out_2, controlled_buffer_1_out}), .en(1'b1), .Q(register_1_q), .clk(clock_1_out));  // open: clr
  Register register_2 (
    .D({controlled_buffer_1_out_2, controlled_buffer_1_out}), .en(1'b0), .Q(register_2_q), .clk(clock_1_out));  // open: clr
  TTY tty_1 (.data(register_1_q[6:0]), .clk(clock_1_out), .we(register_2_q[1]));  // open: clr
  Keyboard keyboard_1 (.clk(clock_1_out), .re(register_2_q[0]), .data(keyboard_1_data));  // open: clr, avail
  assign {controlled_buffer_1_out_2, controlled_buffer_1_out} = 1'b1 ? {1'b0, keyboard_1_data} : 8'bz;  // Controlled_Buffer controlled_buffer_2
  Hex_Digit_Display hex_digit_display_1 (.value(controlled_buffer_1_out_2));  // open: dp
  Hex_Digit_Display hex_digit_display_2 (.value(controlled_buffer_1_out));  // open: dp

  // Notes on the sheet:
  //   Literal to BUS
  //   Set IO1 TTY
  //   Set IO2 Enable TTY (2) & KEY (1)
  //   KEYB to BUS
endmodule
